// Logisim project 4-Bit-alu.circ as structural Verilog: 1 circuit, main circuit main
module main (
  input  F0,
  input  Enable_Input,
  input  A3,
  input  A2,
  input  F1,
  input  A1,
  input  A0,
  input  Enable_Input_2,
  input  B3,
  input  B2,
  input  B1,
  input  B0,
  input  Subtract
);

  wire A0_q, A1_q, A2_q, A3_q, adder_1_cout, adder_1_out, adder_2_cout, adder_2_out, adder_3_cout,
       adder_3_out, adder_4_cout, adder_4_out, B0_q, B1_q, B2_q, B3_q, Clear_2_out, Clear_out, xor_1_out,
       xor_2_out, xor_3_out, xor_4_out, xor_5_out, xor_6_out, xor_7_out, xor_8_out, xor_9_out, xor_10_out,
       xor_11_out, xor_12_out;

  Button Clock (.out(A1));
  Button Clear (.out(Clear_out));
  Button Clear_2 (.out(Clear_2_out));
  D_Flip_Flop u_A3 (.clk(A1), .D(A3), .Q(A3_q), .en(Enable_Input), .reset(Clear_out));  // open: Qn, preset
  D_Flip_Flop u_B3 (.clk(A1), .D(B3), .Q(B3_q), .en(Enable_Input_2), .reset(Clear_2_out));  // open: Qn, preset
  D_Flip_Flop u_A2 (.clk(A1), .D(A2), .Q(A2_q), .en(Enable_Input), .reset(Clear_out));  // open: Qn, preset
  D_Flip_Flop u_B2 (.clk(A1), .D(B2), .Q(B2_q), .en(Enable_Input_2), .reset(Clear_2_out));  // open: Qn, preset
  D_Flip_Flop u_A1 (.clk(A1), .D(A1), .Q(A1_q), .en(Enable_Input));  // open: Qn, preset, reset
  D_Flip_Flop u_B1 (.clk(A1), .D(B1), .Q(B1_q), .en(Enable_Input_2));  // open: Qn, preset, reset
  xor xor_1 (xor_1_out, Subtract, xor_9_out);
  xor xor_2 (xor_2_out, Subtract, xor_10_out);
  xor xor_3 (xor_3_out, Subtract, xor_11_out);
  xor xor_4 (xor_4_out, Subtract, xor_12_out);
  D_Flip_Flop u_A0 (.clk(A1), .D(A0), .Q(A0_q), .en(Enable_Input), .reset(Clear_out));  // open: Qn, preset
  D_Flip_Flop u_B0 (.clk(A1), .D(B0), .Q(B0_q), .en(Enable_Input_2), .reset(Clear_2_out));  // open: Qn, preset
  Adder #(.width(1)) adder_1 (.a(xor_5_out), .b(xor_1_out), .out(adder_1_out), .cin(Subtract), .cout(adder_1_cout));
  Adder #(.width(1)) adder_2 (.a(xor_6_out), .b(xor_2_out), .out(adder_2_out), .cin(adder_1_cout), .cout(adder_2_cout));
  Adder #(.width(1)) adder_3 (.a(xor_7_out), .b(xor_3_out), .out(adder_3_out), .cin(adder_2_cout), .cout(adder_3_cout));
  Adder #(.width(1)) adder_4 (.a(xor_8_out), .b(xor_4_out), .out(adder_4_out), .cin(adder_3_cout), .cout(adder_4_cout));
  xor xor_5 (xor_5_out, F0, A3_q);
  xor xor_6 (xor_6_out, F0, A2_q);
  xor xor_7 (xor_7_out, F0, A1_q);
  xor xor_8 (xor_8_out, F0, A0_q);
  xor xor_9 (xor_9_out, F1, B3_q);
  xor xor_10 (xor_10_out, F1, B2_q);
  xor xor_11 (xor_11_out, F1, B1_q);
  xor xor_12 (xor_12_out, F1, B0_q);
  // AND_Gate and_1 has open pins: in0=xor_5_out, in1=xor_9_out, out=open
  // AND_Gate and_2 has open pins: in0=xor_6_out, in1=xor_10_out, out=open
  // AND_Gate and_3 has open pins: in0=xor_7_out, in1=xor_11_out, out=open
  // AND_Gate and_4 has open pins: in0=xor_8_out, in1=xor_12_out, out=open
  // OR_Gate or_1 has open pins: in0=xor_5_out, in1=xor_9_out, out=open
  // OR_Gate or_2 has open pins: in0=xor_6_out, in1=xor_10_out, out=open
  // OR_Gate or_3 has open pins: in0=xor_7_out, in1=xor_11_out, out=open
  // OR_Gate or_4 has open pins: in0=xor_8_out, in1=xor_12_out, out=open
  // XOR_Gate xor_13 has open pins: in0=xor_5_out, in1=xor_9_out, out=open
  // XOR_Gate xor_14 has open pins: in0=xor_6_out, in1=xor_10_out, out=open
  // XOR_Gate xor_15 has open pins: in0=xor_7_out, in1=xor_11_out, out=open
  // XOR_Gate xor_16 has open pins: in0=xor_8_out, in1=xor_12_out, out=open

  // Notes on the sheet:
  //   F0: !A
  //   F1: !B
endmodule
